// Logisim project lab0.circ as structural Verilog: 3 circuits, main circuit main
module main (
  input  [7:0] A,
  input  [7:0] B,
  output Sum
);

  wire [7:0] adder_1_out;
  wire [8:0] add_eight_1_sum, xor_1_out;
  wire [8:8] adder_1_cout;

  Adder adder_1 (.a(A), .b(B), .out(adder_1_out), .cout(adder_1_cout[8]));  // open: cin
  add_eight add_eight_1 (.A(A), .B(B), .Sum(add_eight_1_sum));
  assign xor_1_out = add_eight_1_sum ^ {adder_1_cout[8], adder_1_out};  // XOR_Gate xor_1, 9 bits wide
  nor nor_1 (Sum, xor_1_out[0], xor_1_out[1], xor_1_out[2], xor_1_out[3], xor_1_out[4], xor_1_out[5], xor_1_out[6], xor_1_out[7], xor_1_out[8]);
endmodule

module add_binary (
  input  A,
  input  B,
  input  C_in,
  output Sum,
  output C_out
);

  wire and_1_out, and_2_out, xor_1_out;

  xor xor_1 (xor_1_out, A, B);
  and and_1 (and_1_out, xor_1_out, C_in);
  and and_2 (and_2_out, A, B);
  xor xor_2 (Sum, xor_1_out, C_in);
  or or_1 (C_out, and_1_out, and_2_out);
endmodule

module add_eight (
  input  [7:0] A,
  input  [7:0] B,
  output [8:0] Sum
);

  wire add_binary_1_c_out, add_binary_2_c_out, add_binary_3_c_out, add_binary_4_c_out, add_binary_5_c_out,
       add_binary_6_c_out, add_binary_7_c_out;

  add_binary add_binary_1 (.A(A[0]), .B(B[0]), .C_in(1'b0), .Sum(Sum[0]), .C_out(add_binary_1_c_out));
  add_binary add_binary_2 (.A(A[1]), .B(B[1]), .C_in(add_binary_1_c_out), .Sum(Sum[1]), .C_out(add_binary_2_c_out));
  add_binary add_binary_3 (.A(A[2]), .B(B[2]), .C_in(add_binary_2_c_out), .Sum(Sum[2]), .C_out(add_binary_3_c_out));
  add_binary add_binary_4 (.A(A[3]), .B(B[3]), .C_in(add_binary_3_c_out), .Sum(Sum[3]), .C_out(add_binary_4_c_out));
  add_binary add_binary_5 (.A(A[4]), .B(B[4]), .C_in(add_binary_4_c_out), .Sum(Sum[4]), .C_out(add_binary_5_c_out));
  add_binary add_binary_6 (.A(A[5]), .B(B[5]), .C_in(add_binary_5_c_out), .Sum(Sum[5]), .C_out(add_binary_6_c_out));
  add_binary add_binary_7 (.A(A[6]), .B(B[6]), .C_in(add_binary_6_c_out), .Sum(Sum[6]), .C_out(add_binary_7_c_out));
  add_binary add_binary_8 (.A(A[7]), .B(B[7]), .C_in(add_binary_7_c_out), .Sum(Sum[7]), .C_out(Sum[8]));
endmodule
